# Fritzing sketch rx_rpi (saved by Fritzing 0.9.3b)

parts:
  Raspberry_Pi = Raspberry Pi 3 [part_number=RPI-3-V1.2]
  Remote_Receiver = IC, SIP package, 3 pins

nets:
  3V3: Raspberry_Pi.3v3, Raspberry_Pi.3V3, Remote_Receiver.pin1
  N1: Raspberry_Pi.GND, Remote_Receiver.pin2
  N2: Raspberry_Pi.GPIO15, Remote_Receiver.pin3

notes:
  Remote Receiver
  3.3V
  GND
  DATA
